// Logisim project cpu.circ as structural Verilog: 1 circuit, main circuit cpu
module cpu (
  input  clk,
  input  [31:0] INSTRUCTION,
  input  [31:0] READ_DATA,
  output [31:0] WRITE_ADDRESS,
  output [31:0] PROGRAM_COUNTER,
  output [31:0] ra,
  output [31:0] sp,
  output [31:0] t0,
  output [31:0] t1,
  output [31:0] t2,
  output [31:0] s0,
  output [31:0] s1,
  output [31:0] a0,
  output [31:0] tohost,
  output [3:0] WRITE_ENABLE,
  output [31:0] WRITE_DATA
);

  wire branch_comp_1_breq, branch_comp_1_brlt, control_logic_1_asel, control_logic_1_brun,
       control_logic_1_bsel, control_logic_1_pcsel, control_logic_1_regwen;
  wire [1:0] control_logic_1_wbsel;
  wire [2:0] control_logic_1_immsel;
  wire [3:0] control_logic_1_alusel;
  wire [31:0] adder_1_out, imm_gen_1_imm, multiplexer_1_out, multiplexer_2_out, multiplexer_3_out,
       multiplexer_4_out, PCplus4, regfile_1_read_data_1, register_1_q;

  Adder #(.width(32)) adder_1 (.a(PROGRAM_COUNTER), .b(32'h4), .out(adder_1_out));  // open: cin, cout
  Multiplexer #(.enable("false"), .width(32)) multiplexer_1 (
    .in0(adder_1_out), .in1(WRITE_ADDRESS), .out(multiplexer_1_out), .sel(control_logic_1_pcsel));
  Register #(.width(32)) PC (.D(multiplexer_1_out), .clk(clk), .Q(PROGRAM_COUNTER));  // open: en, clr
  Register #(.width(32)) register_1 (.D(INSTRUCTION), .en(1'b1), .clk(clk), .Q(register_1_q));  // open: clr
  Register #(.width(32)) register_2 (.D(adder_1_out), .en(1'b1), .clk(clk), .Q(PCplus4));  // open: clr
  control_logic control_logic_1 (
    .PCSel(control_logic_1_pcsel), .RegWEn(control_logic_1_regwen), .ImmSel(control_logic_1_immsel),
    .BrUn(control_logic_1_brun), .ASel(control_logic_1_asel), .BSel(control_logic_1_bsel),
    .ALUSel(control_logic_1_alusel), .MemRW(WRITE_ENABLE[3]), .WBSel(control_logic_1_wbsel),
    .inst(register_1_q), .BrEq(branch_comp_1_breq), .BrLt(branch_comp_1_brlt));  // open: CSRWen, CSRSel
  regfile regfile_1 (
    .rs1(register_1_q[19:15]), .rs2(register_1_q[24:20]), .rd(register_1_q[11:7]),
    .Write_Data(multiplexer_4_out), .RegWEn(control_logic_1_regwen), .clk(clk), .ra(ra), .sp(sp), .t0(t0),
    .t1(t1), .t2(t2), .s0(s0), .s1(s1), .a0(a0), .Read_Data_1(regfile_1_read_data_1), .Read_Data_2(WRITE_DATA));
  imm_gen imm_gen_1 (.inst(register_1_q), .ImmSel(control_logic_1_immsel), .imm(imm_gen_1_imm));
  Multiplexer #(.enable("false"), .width(32)) multiplexer_2 (
    .in0(PROGRAM_COUNTER), .in1(regfile_1_read_data_1), .out(multiplexer_2_out), .sel(control_logic_1_asel));
  Multiplexer #(.enable("false"), .width(32)) multiplexer_3 (
    .in0(WRITE_DATA), .in1(imm_gen_1_imm), .out(multiplexer_3_out), .sel(control_logic_1_bsel));
  branch_comp branch_comp_1 (
    .rs1(regfile_1_read_data_1), .rs2(WRITE_DATA), .BrUn(control_logic_1_brun), .BrEq(branch_comp_1_breq),
    .BrLt(branch_comp_1_brlt));
  alu alu_1 (.Result(WRITE_ADDRESS), .A(multiplexer_2_out), .B(multiplexer_3_out), .ALUSel(control_logic_1_alusel));
  Multiplexer #(.enable("false"), .select(2), .width(32)) multiplexer_4 (
    .in0(PCplus4), .in1(WRITE_ADDRESS), .in2(READ_DATA), .out(multiplexer_4_out), .sel(control_logic_1_wbsel));  // open: in3
  csr csr_1 (.tohost(tohost));  // open: CSR_address, CSR_din, CSR_WE, clk

  assign WRITE_ENABLE[2:0] = {3{WRITE_ENABLE[3]}};

  // Other names for the same wires on the sheet: ALURes[31:0] = WRITE_ADDRESS

  // Notes on the sheet:
  //   Output to IMEM
  //   IMEM (do **NOT** move this)
  //   Inputs from IMEM
  //   Inputs/Outputs for testing. Do **NOT** move these.
  //   PC
  //   rs1
  //   rs2
  //   imm
  //   Outputs To DMEM
  //   DMEM (do **NOT** move this)
  //   Inputs From DMEM
endmodule
